// Logisim project 1.circ as structural Verilog: 3 circuits, main circuit main
module main (
  input  [7:0] subtractor,
  input  [7:0] subtractible,
  input  in_3,
  output [7:0] out_4,
  output [7:0] out_5,
  output [7:0] difference,
  output [7:0] out_7,
  output out_8
);

  wire subtractor_3_inputs_1_offset, subtractor_3_inputs_2_offset, subtractor_3_inputs_3_offset,
       subtractor_3_inputs_4_offset, subtractor_3_inputs_5_offset, subtractor_3_inputs_6_offset,
       subtractor_3_inputs_7_offset;

  subtractor_3_inputs subtractor_3_inputs_1 (
    .A(subtractible[0]), .B(subtractor[0]), .C(in_3), .diff(difference[0]),
    .offset(subtractor_3_inputs_1_offset));
  subtractor_3_inputs subtractor_3_inputs_2 (
    .A(subtractible[1]), .B(subtractor[1]), .C(subtractor_3_inputs_1_offset), .diff(difference[1]),
    .offset(subtractor_3_inputs_2_offset));
  subtractor_3_inputs subtractor_3_inputs_3 (
    .A(subtractible[2]), .B(subtractor[2]), .C(subtractor_3_inputs_2_offset), .diff(difference[2]),
    .offset(subtractor_3_inputs_3_offset));
  subtractor_3_inputs subtractor_3_inputs_4 (
    .A(subtractible[3]), .B(subtractor[3]), .C(subtractor_3_inputs_3_offset), .diff(difference[3]),
    .offset(subtractor_3_inputs_4_offset));
  subtractor_3_inputs subtractor_3_inputs_5 (
    .A(subtractible[4]), .B(subtractor[4]), .C(subtractor_3_inputs_4_offset), .diff(difference[4]),
    .offset(subtractor_3_inputs_5_offset));
  subtractor_3_inputs subtractor_3_inputs_6 (
    .A(subtractible[5]), .B(subtractor[5]), .C(subtractor_3_inputs_5_offset), .diff(difference[5]),
    .offset(subtractor_3_inputs_6_offset));
  subtractor_3_inputs subtractor_3_inputs_7 (
    .A(subtractible[6]), .B(subtractor[6]), .C(subtractor_3_inputs_6_offset), .diff(difference[6]),
    .offset(subtractor_3_inputs_7_offset));
  subtractor_3_inputs subtractor_3_inputs_8 (
    .A(subtractible[7]), .B(subtractor[7]), .C(subtractor_3_inputs_7_offset), .diff(difference[7]),
    .offset(out_8));

  assign out_4 = subtractor;
  assign out_5 = difference;
  assign out_7 = subtractible;
endmodule

module subtractor_3_inputs (
  input  A,
  input  B,
  input  C,
  output diff,
  output offset
);

  wire and_1_out, and_2_out, and_3_out, and_4_out, and_5_out, and_6_out, and_7_out, not_1_out, not_2_out,
       not_3_out;

  not not_1 (not_1_out, A);
  not not_2 (not_2_out, B);
  not not_3 (not_3_out, C);
  and and_1 (and_1_out, not_1_out, not_2_out, C);
  and and_2 (and_2_out, not_1_out, B, not_3_out);
  and and_3 (and_3_out, A, not_2_out, not_3_out);
  and and_4 (and_4_out, A, B, C);
  and and_5 (and_5_out, B, C);
  and and_6 (and_6_out, not_1_out, B);
  and and_7 (and_7_out, not_1_out, C);
  or or_1 (offset, and_5_out, and_6_out, and_7_out);
  or or_2 (diff, and_1_out, and_2_out, and_3_out, and_4_out);
endmodule

module shift (
  input  [3:0] ABCD,
  output [3:0] out_2,
  output [3:0] result,
  output [3:0] out_4
);

  wire and_1_out, and_2_out, and_3_out, and_4_out, and_5_out, and_6_out, and_7_out, and_8_out, and_9_out,
       and_10_out, not_1_out, not_2_out, not_3_out;

  not not_1 (not_1_out, ABCD[3]);
  not not_2 (not_2_out, ABCD[2]);
  not not_3 (not_3_out, ABCD[1]);
  not not_4 (out_4[0], ABCD[0]);
  and and_1 (and_1_out, not_1_out, out_4[0]);
  and and_2 (and_2_out, not_1_out, not_2_out);
  and and_3 (and_3_out, not_1_out, not_3_out);
  and and_4 (and_4_out, ABCD[3], ABCD[2], ABCD[1], ABCD[0]);
  and and_5 (and_5_out, ABCD[2], not_3_out);
  and and_6 (and_6_out, ABCD[2], out_4[0]);
  and and_7 (and_7_out, not_2_out, ABCD[1], ABCD[0]);
  and and_8 (and_8_out, ABCD[1], out_4[0]);
  and and_9 (and_9_out, not_1_out, not_3_out, ABCD[0]);
  and and_10 (and_10_out, ABCD[2], not_3_out, ABCD[0]);
  or or_1 (out_4[3], and_1_out, and_2_out, and_3_out, and_4_out);
  or or_2 (out_4[2], and_5_out, and_6_out, and_7_out);
  or or_3 (out_4[1], and_8_out, and_9_out, and_10_out);

  assign out_2 = ABCD;
  assign result = out_4;
endmodule
